// Logisim project labo_alu_etu.circ as structural Verilog: 13 circuits, main circuit ALU_MAXV
module ALU_MAXV (
  input  [3:0] a_i,
  input  [3:0] b_i,
  output [3:0] c_o,
  output erreur_o
);

  wire [5:0] opcode_i_sw6;

  DipSwitch opcode_i (
    .sw1(opcode_i_sw6[5]), .sw2(opcode_i_sw6[4]), .sw3(opcode_i_sw6[3]), .sw4(opcode_i_sw6[2]),
    .sw5(opcode_i_sw6[1]), .sw6(opcode_i_sw6[0]));  // open: sw7, sw8
  ALU_Top alu_inst (.a_i(a_i), .b_i(b_i), .op_i(opcode_i_sw6), .c_o(c_o), .erreur_o(erreur_o));

  // Notes on the sheet:
  //   Attention, votre version de Logisim
  //   ne contient pas de tracker. Si vous
  //   enregistrez votre projet, toutes les
  //   informations du tracker seront
  //   définitivement effacées.
endmodule

module ALU_Top (
  input  [3:0] a_i,
  input  [3:0] b_i,
  input  [5:0] op_i,
  output [3:0] c_o,
  output erreur_o
);

  wire add_sub4bits_1_carry_o, add_sub4bits_1_negative_o, add_sub4bits_1_zero_o;
  wire [3:0] add_sub4bits_1_r_o, comparateur_1_cmp_o, custom_1_s_o, unitelogique_1_f_o;

  Add_Sub4Bits add_sub4bits_1 (
    .a_i(a_i), .b_i(b_i), .op_i(op_i[3:2]), .r_o(add_sub4bits_1_r_o), .carry_o(add_sub4bits_1_carry_o),
    .Negative_o(add_sub4bits_1_negative_o), .zero_o(add_sub4bits_1_zero_o));  // open: overflow_o
  Comparateur comparateur_1 (
    .carry_i(add_sub4bits_1_carry_o), .Negative_i(add_sub4bits_1_negative_o), .zero_i(add_sub4bits_1_zero_o),
    .a_i(a_i[3]), .b_i(b_i[3]), .op_i(op_i[2:0]), .cmp_o(comparateur_1_cmp_o));
  UniteLogique unitelogique_1 (.a_i(a_i), .b_i(b_i), .op_i(op_i[1:0]), .f_o(unitelogique_1_f_o));
  Custom custom_1 (.a_i(a_i), .s_o(custom_1_s_o));
  Multiplexer #(.select(2), .width(4), .enable("false")) multiplexer_1 (
    .in0(add_sub4bits_1_r_o), .in1(comparateur_1_cmp_o), .in2(unitelogique_1_f_o), .in3(custom_1_s_o),
    .out(c_o), .sel(op_i[5:4]));
  Opcode_error opcode_error_1 (.op_i(op_i), .erreur_o(erreur_o));

  // Other names for the same wires on the sheet: a_i_bit3 = a_i[3]; b_i_bit3 = b_i[3]

  // Notes on the sheet:
  //   Attention, votre version de Logisim
  //   ne contient pas de tracker. Si vous
  //   enregistrez votre projet, toutes les
  //   informations du tracker seront
  //   définitivement effacées.
endmodule

module Add_Sub4Bits (
  input  [3:0] a_i,
  input  [3:0] b_i,
  input  [1:0] op_i,
  output [3:0] r_o,
  output overflow_o,
  output carry_o,
  output Negative_o,
  output zero_o
);

  wire add4bit_1_c_o, and_1_out, and_2_out, decoder_1_out0, decoder_1_out2, decoder_1_out3, or_1_out;
  wire [3:0] xor_1_out;
  wire [3:3] or_2_out;

  Decoder #(.select(2), .enable("false")) decoder_1 (
    .out0(decoder_1_out0), .out2(decoder_1_out2), .out3(decoder_1_out3), .sel(op_i));  // open: out1
  or or_1 (or_1_out, decoder_1_out0, decoder_1_out2);
  or or_2 (or_2_out[3], decoder_1_out2, decoder_1_out3);
  assign xor_1_out = b_i ^ {4{or_2_out[3]}};  // XOR_Gate xor_1, 4 bits wide
  Add4bit add4bit_1 (.c_i(or_2_out[3]), .a_i(a_i), .b_i(xor_1_out), .r_o(r_o), .c_o(add4bit_1_c_o));
  xor xor_2 (carry_o, or_2_out[3], add4bit_1_c_o);
  and and_1 (and_1_out, or_1_out, r_o[3]);
  and and_2 (and_2_out, add4bit_1_c_o, or_1_out);
  Multiplexer #(.enable("false")) multiplexer_1 (.in0(and_1_out), .in1(and_2_out), .out(Negative_o), .sel(overflow_o));
  Overflow overflow_1 (
    .a_neg_i(a_i[3]), .b_neg_i(b_i[3]), .r_neg_i(r_o[3]), .sous_i(or_2_out[3]), .signe_i(or_1_out),
    .carry_i(carry_o), .overflow_o(overflow_o));
  nor nor_1 (zero_o, r_o[0], r_o[1], r_o[2], r_o[3], overflow_o);

  // Other names for the same wires on the sheet: a_i_Bit3 = a_i[3]; b_i_Bit3 = b_i[3]; r_o_Bit3 = r_o[3]

  // Notes on the sheet:
  //   Attention, votre version de Logisim
  //   ne contient pas de tracker. Si vous
  //   enregistrez votre projet, toutes les
  //   informations du tracker seront
  //   définitivement effacées.
  //   Soustraction pour 10 et 11
  //   Signé pour 00 et 10, non signé pour 01 et 11
  //   SIgné
  //   Soustraction
endmodule

module Comparateur (
  input  carry_i,
  input  Negative_i,
  input  zero_i,
  input  a_i,
  input  b_i,
  input  [2:0] op_i,
  output [3:0] cmp_o
);

  wire and_1_out, and_2_out, and_3_out, and_4_out, and_5_out, and_6_out, decoder_1_out1, decoder_1_out2,
       decoder_1_out3, decoder_1_out4, decoder_1_out5, decoder_1_out6, not_1_out, not_2_out, not_3_out;

  Decoder #(.select(3), .enable("false")) decoder_1 (
    .out1(decoder_1_out1), .out2(decoder_1_out2), .out3(decoder_1_out3), .out4(decoder_1_out4),
    .out5(decoder_1_out5), .out6(decoder_1_out6), .sel(op_i));  // open: out0, out7
  not not_1 (not_1_out, Negative_i);
  not not_2 (not_2_out, zero_i);
  not not_3 (not_3_out, carry_i);
  and and_1 (and_1_out, not_1_out, decoder_1_out1);
  and and_2 (and_2_out, Negative_i, decoder_1_out2);
  and and_3 (and_3_out, not_2_out, decoder_1_out3);
  and and_4 (and_4_out, zero_i, decoder_1_out4);
  and and_5 (and_5_out, carry_i, decoder_1_out5);
  and and_6 (and_6_out, not_3_out, decoder_1_out6);
  or or_1 (cmp_o[0], and_1_out, and_2_out, and_3_out, and_4_out, and_5_out, and_6_out);

  assign cmp_o[3:1] = 3'b000;

  // Notes on the sheet:
  //   Attention, votre version de Logisim
  //   ne contient pas de tracker. Si vous
  //   enregistrez votre projet, toutes les
  //   informations du tracker seront
  //   définitivement effacées.
  //   001 : not(Negative) signé
  //   010 : Negative signé
  //   011 : not(Zero)
  //   100 : Zero
  //   101 : Carry non signé
  //   110 : not(Carry) non signé
endmodule

module UniteLogique (
  input  [3:0] a_i,
  input  [3:0] b_i,
  input  [1:0] op_i,
  output [3:0] f_o
);

  wire [3:0] and_1_out, nand_1_out, or_1_out, xor_1_out;

  assign and_1_out = a_i & b_i;  // AND_Gate and_1, 4 bits wide
  assign or_1_out = a_i | b_i;  // OR_Gate or_1, 4 bits wide
  assign nand_1_out = ~(a_i & b_i);  // NAND_Gate nand_1, 4 bits wide
  assign xor_1_out = a_i ^ b_i;  // XOR_Gate xor_1, 4 bits wide
  Multiplexer #(.select(2), .width(4), .enable("false")) multiplexer_1 (
    .in0(and_1_out), .in1(or_1_out), .in2(nand_1_out), .in3(xor_1_out), .out(f_o), .sel(op_i));

  // Notes on the sheet:
  //   Attention, votre version de Logisim
  //   ne contient pas de tracker. Si vous
  //   enregistrez votre projet, toutes les
  //   informations du tracker seront
  //   définitivement effacées.
endmodule

module Custom (
  input  [3:0] a_i,
  output [3:0] s_o
);

  wire and_1_out, and_2_out, not_1_out, not_2_out, not_3_out, not_4_out, xor_1_out, xor_2_out;

  not not_1 (not_1_out, a_i[0]);
  not not_2 (not_2_out, a_i[1]);
  not not_3 (not_3_out, a_i[2]);
  not not_4 (not_4_out, a_i[3]);
  and and_1 (and_1_out, not_1_out, not_2_out, xor_2_out);
  xor xor_1 (xor_1_out, a_i[0], a_i[1]);
  xor xor_2 (xor_2_out, a_i[2], a_i[3]);
  and and_2 (and_2_out, xor_1_out, not_3_out, not_4_out);
  or or_1 (s_o[0], and_1_out, and_2_out);

  assign s_o[3:1] = 3'b000;

  // Notes on the sheet:
  //   Attention, votre version de Logisim
  //   ne contient pas de tracker. Si vous
  //   enregistrez votre projet, toutes les
  //   informations du tracker seront
  //   définitivement effacées.
  //   Devient (A/B + /AB)/C/D + (C/D + /CD)/A/B
  //   Devient (A^B)/C/D + (C^D)/A/B
  //   Simplification de l'équation A/B/C/D + /AB/C/D + /A/BC/D + /A/B/CD
endmodule

module Add1bit (
  input  a_i,
  input  b_i,
  input  c_i,
  output r_o,
  output c_o
);

  wire and_1_out, and_2_out, and_3_out, xor_1_out;

  xor xor_1 (xor_1_out, a_i, b_i);
  and and_1 (and_1_out, a_i, b_i);
  and and_2 (and_2_out, a_i, c_i);
  and and_3 (and_3_out, b_i, c_i);
  xor xor_2 (r_o, xor_1_out, c_i);
  or or_1 (c_o, and_1_out, and_2_out, and_3_out);

  // Notes on the sheet:
  //   Attention, votre version de Logisim
  //   ne contient pas de tracker. Si vous
  //   enregistrez votre projet, toutes les
  //   informations du tracker seront
  //   définitivement effacées.
endmodule

module Add4bit (
  input  c_i,
  input  [3:0] a_i,
  input  [3:0] b_i,
  output [3:0] r_o,
  output c_o
);

  wire add1bit_1_c_o, add1bit_2_c_o, add1bit_3_c_o;

  Add1bit add1bit_1 (.a_i(a_i[0]), .b_i(b_i[0]), .c_i(c_i), .r_o(r_o[0]), .c_o(add1bit_1_c_o));
  Add1bit add1bit_2 (.a_i(a_i[1]), .b_i(b_i[1]), .c_i(add1bit_1_c_o), .r_o(r_o[1]), .c_o(add1bit_2_c_o));
  Add1bit add1bit_3 (.a_i(a_i[2]), .b_i(b_i[2]), .c_i(add1bit_2_c_o), .r_o(r_o[2]), .c_o(add1bit_3_c_o));
  Add1bit add1bit_4 (.a_i(a_i[3]), .b_i(b_i[3]), .c_i(add1bit_3_c_o), .r_o(r_o[3]), .c_o(c_o));

  // Notes on the sheet:
  //   Attention, votre version de Logisim
  //   ne contient pas de tracker. Si vous
  //   enregistrez votre projet, toutes les
  //   informations du tracker seront
  //   définitivement effacées.
endmodule

module AllOrNothing (
  input  a_i,
  input  b_i,
  input  c_i,
  output r_o
);

  wire xnor_1_out, xnor_2_out;

  xnor xnor_1 (xnor_1_out, a_i, b_i);
  xnor xnor_2 (xnor_2_out, b_i, c_i);
  and and_1 (r_o, xnor_1_out, xnor_2_out);

  // Notes on the sheet:
  //   Attention, votre version de Logisim
  //   ne contient pas de tracker. Si vous
  //   enregistrez votre projet, toutes les
  //   informations du tracker seront
  //   définitivement effacées.
endmodule

module Overflow (
  input  a_neg_i,
  input  b_neg_i,
  input  r_neg_i,
  input  sous_i,
  input  signe_i,
  input  carry_i,
  output overflow_o
);

  wire and_1_out, and_2_out, and_3_out, and_4_out, and_5_out, and_6_out, not_1_out, not_2_out, not_3_out,
       not_4_out, not_5_out, not_6_out, not_7_out, not_8_out, not_9_out, or_1_out;

  not not_1 (not_1_out, a_neg_i);
  not not_2 (not_2_out, b_neg_i);
  not not_3 (not_3_out, sous_i);
  not not_4 (not_4_out, r_neg_i);
  not not_5 (not_5_out, sous_i);
  not not_6 (not_6_out, a_neg_i);
  not not_7 (not_7_out, b_neg_i);
  not not_8 (not_8_out, r_neg_i);
  and and_1 (and_1_out, not_1_out, not_2_out, r_neg_i, not_3_out);
  and and_2 (and_2_out, a_neg_i, b_neg_i, not_4_out, not_5_out);
  and and_3 (and_3_out, not_6_out, b_neg_i, r_neg_i, sous_i);
  and and_4 (and_4_out, a_neg_i, not_7_out, not_8_out, sous_i);
  or or_1 (or_1_out, and_1_out, and_2_out, and_3_out, and_4_out);
  and and_5 (and_5_out, or_1_out, signe_i);
  not not_9 (not_9_out, signe_i);
  and and_6 (and_6_out, not_9_out, carry_i);
  or or_2 (overflow_o, and_5_out, and_6_out);

  // Notes on the sheet:
  //   Attention, votre version de Logisim
  //   ne contient pas de tracker. Si vous
  //   enregistrez votre projet, toutes les
  //   informations du tracker seront
  //   définitivement effacées.
endmodule

module Opcode_error (
  input  [5:0] op_i,
  output erreur_o
);

  wire and_1_out, and_2_out, and_3_out, and_4_out, and_5_out, and_6_out, not_1_out, not_2_out, not_3_out,
       not_4_out, not_5_out;

  not not_1 (not_1_out, op_i[0]);
  not not_2 (not_2_out, op_i[1]);
  not not_3 (not_3_out, op_i[2]);
  not not_4 (not_4_out, op_i[3]);
  and and_1 (and_1_out, op_i[4], not_5_out);
  not not_5 (not_5_out, op_i[5]);
  and and_2 (and_2_out, op_i[0], op_i[1], op_i[2]);
  and and_3 (and_3_out, not_1_out, not_2_out, not_3_out);
  and and_4 (and_4_out, not_4_out, and_1_out);
  and and_5 (and_5_out, and_2_out, and_1_out);
  and and_6 (and_6_out, and_3_out, and_1_out);
  or or_1 (erreur_o, and_5_out, and_6_out, and_4_out);

  // Notes on the sheet:
  //   Attention, votre version de Logisim
  //   ne contient pas de tracker. Si vous
  //   enregistrez votre projet, toutes les
  //   informations du tracker seront
  //   définitivement effacées.
  //   010xxx
  //   011111
  //   011000
endmodule

module Chronogram (
  output [3:0] cmp_o
);

  wire clk_out;
  wire [7:0] counter_1_q;

  Clock clk (.out(clk_out));
  Clock sysclk ();  // open: out
  Counter counter_1 (
    .clr(1'b0), .load(1'b0), .up(1'b1), .count(1'b1), .clk(clk_out), .D({8{1'b0}}), .Q(counter_1_q));  // open: carry
  Comparateur comparateur_1 (
    .carry_i(counter_1_q[0]), .Negative_i(counter_1_q[1]), .zero_i(counter_1_q[2]), .a_i(counter_1_q[3]),
    .b_i(counter_1_q[4]), .op_i(counter_1_q[7:5]), .cmp_o(cmp_o));

  // Notes on the sheet:
  //   Attention, votre version de Logisim
  //   ne contient pas de tracker. Si vous
  //   enregistrez votre projet, toutes les
  //   informations du tracker seront
  //   définitivement effacées.
endmodule

module TestCmp (
  input  a_i,
  input  b_i,
  input  neg_i,
  output o
);

  wire and_1_out, and_2_out, and_3_out, not_1_out, not_2_out, not_3_out, not_4_out;

  not not_1 (not_1_out, a_i);
  not not_2 (not_2_out, neg_i);
  not not_3 (not_3_out, a_i);
  not not_4 (not_4_out, neg_i);
  and and_1 (and_1_out, not_1_out, not_2_out);
  and and_2 (and_2_out, not_3_out, b_i);
  and and_3 (and_3_out, b_i, not_4_out);
  or or_1 (o, and_1_out, and_2_out, and_3_out);

  // Notes on the sheet:
  //   Attention, votre version de Logisim
  //   ne contient pas de tracker. Si vous
  //   enregistrez votre projet, toutes les
  //   informations du tracker seront
  //   définitivement effacées.
endmodule
